# Fritzing sketch Wiring (saved by Fritzing 0.9.4)

parts:
  Bauteil1 = Arduino Nano (Rev3.0)
  NEOPIXEL1 = Neopixel Strip -- Black (30/m) [part_number=1376]
  S1 = Pushbutton [package="[THT]"]
  R2 = Resistor [tolerance=±5% resistance=1k package=THT]

nets:
  N1: Bauteil1.GND, R2.Pin_0
  N2: Bauteil1.D2, S1.Pin_3, R2.Pin_1
  N3: Bauteil1.D6, NEOPIXEL1.Din
  5V: Bauteil1.5V, NEOPIXEL1.+5V

notes:
  5V DC power source

custom parts:
  Neopixel Strip -- Black (30/m): These NeoPixel strips have 30 digitally-addressable pixel LEDs per meter and are very affordable and are only 12.5 mm wide, 10 mm if you remove the strip from the casing.
